// Logisim project Project1Given.circ as structural Verilog: 5 circuits, main circuit main
module main (
  input  in_1,
  input  in_2,
  input  in_3,
  input  in_4,
  input  Five,
  output N,
  output E,
  output [3:0] out_8
);

  wire fiveseven_1_a, fiveseven_1_b, fiveseven_1_c, fiveseven_1_d, fiveseven_1_e, fiveseven_1_f,
       fiveseven_1_g;

  Compare compare_1 (.X0(1'b0), .X1(1'b0), .X2(1'b1), .Y0(1'b0), .Y1(1'b0), .Y2(1'b1), .N(N), .E(E));
  Gray gray_1 (.B0(1'b1), .B1(1'b0), .B2(1'b0), .B3(1'b1), .G0(out_8[0]), .G1(out_8[1]), .G2(out_8[2]), .G3(out_8[3]));
  FiveSeven fiveseven_1 (
    .V(in_1), .W(in_2), .X(in_3), .Y(in_4), .Z(Five), .A(fiveseven_1_a), .B(fiveseven_1_b),
    .C(fiveseven_1_c), .D(fiveseven_1_d), .E(fiveseven_1_e), .F(fiveseven_1_f), .G(fiveseven_1_g));
  _7_Segment_Display u_7_segment_display_1 (
    .g(fiveseven_1_g), .f(fiveseven_1_f), .a(fiveseven_1_a), .b(fiveseven_1_b), .e(fiveseven_1_e),
    .d(fiveseven_1_d), .c(fiveseven_1_c));  // open: dp
endmodule

module Compare (
  input  X0,
  input  X1,
  input  X2,
  input  Y0,
  input  Y1,
  input  Y2,
  output N,
  output E
);

  wire and_2_out, and_3_out, and_4_out, and_5_out, and_6_out, myxnor_1_o, myxnor_2_o, myxnor_3_o, myxnor_4_o,
       myxnor_5_o, myxnor_6_o, not_1_out, not_2_out, not_3_out, not_4_out, not_5_out, not_6_out;

  not not_1 (not_1_out, X0);
  not not_2 (not_2_out, X1);
  not not_3 (not_3_out, X2);
  not not_4 (not_4_out, Y0);
  not not_5 (not_5_out, Y1);
  not not_6 (not_6_out, Y2);
  myXNOR myxnor_1 (.A(Y0), .B(X0), .O(myxnor_1_o));
  myXNOR myxnor_2 (.A(Y1), .B(X1), .O(myxnor_2_o));
  myXNOR myxnor_3 (.A(Y2), .B(X2), .O(myxnor_3_o));
  and and_1 (E, myxnor_1_o, myxnor_2_o, myxnor_3_o);
  and and_2 (and_2_out, not_3_out, Y2);
  myXNOR myxnor_4 (.A(X2), .B(Y2), .O(myxnor_4_o));
  and and_3 (and_3_out, myxnor_4_o, and_4_out);
  and and_4 (and_4_out, not_2_out, Y1);
  myXNOR myxnor_5 (.A(X2), .B(Y2), .O(myxnor_5_o));
  and and_5 (and_5_out, myxnor_5_o, myxnor_6_o, and_6_out);
  myXNOR myxnor_6 (.A(X1), .B(Y1), .O(myxnor_6_o));
  and and_6 (and_6_out, not_1_out, Y0);
  or or_1 (N, and_2_out, and_3_out, and_5_out);
endmodule

module Gray (
  input  B0,
  input  B1,
  input  B2,
  input  B3,
  output G0,
  output G1,
  output G2,
  output G3
);
endmodule

module FiveSeven (
  input  V,
  input  W,
  input  X,
  input  Y,
  input  Z,
  output A,
  output B,
  output C,
  output D,
  output E,
  output F,
  output G
);
endmodule

module myXNOR (
  input  A,
  input  B,
  output O
);

  wire and_1_out, and_2_out, not_1_out, not_2_out, or_1_out;

  not not_1 (not_1_out, A);
  not not_2 (not_2_out, B);
  and and_1 (and_1_out, A, not_2_out);
  and and_2 (and_2_out, not_1_out, B);
  or or_1 (or_1_out, and_2_out, and_1_out);
  not not_3 (O, or_1_out);
endmodule
